// Logisim project gol_16.circ as structural Verilog: 7 circuits, main circuit gol16
module gol16 (
);

  wire aadd, and_1_out, and_2_out, anop, aop, asub, ccoe, clk, clr, coe, ctest, ctrue, frce, froe, ibread,
       ibwrite, iclk, irce, lroe, marce, maroe, mdrce, mdrget, mdroe, mdrput, not_2_out, or_1_out, pcoe, rd,
       regr, regw, rx, ry, si7, si9, spoe, t1ce, t1oe, t2ce, t2oe, ui4, ui7, ui9;
  wire [1:0] controlled_buffer_1_out, instreg_q_2;
  wire [2:0] controlled_buffer_4_out;
  wire [3:0] alu_1_c, cc, reg4_1_q;
  wire [3:2] instreg_q_3;
  wire [4:0] multiplexer_1_out, OpBus;
  wire [15:0] alu_1_r, controlled_buffer_10_out, controlled_buffer_20_out, controlled_buffer_22_out,
       instreg_q, mar_q, mdr_q, reg16_1_q;

  Button button_1 (.out(clr));
  Clock clock_1 (.out(clk));
  assign controlled_buffer_1_out = rd ? instreg_q_3 : 2'bz;  // Controlled_Buffer controlled_buffer_1
  assign OpBus = aop ? instreg_q[15:11] : 5'bz;  // Controlled_Buffer controlled_buffer_2
  not not_1 (iclk, clk);
  or or_1 (or_1_out, rd, rx, ry);
  assign controlled_buffer_1_out = rx ? instreg_q_2 : 2'bz;  // Controlled_Buffer controlled_buffer_3
  assign controlled_buffer_4_out = pcoe ? 3'b100 : 3'bz;  // Controlled_Buffer controlled_buffer_4
  assign controlled_buffer_4_out = or_1_out ? {1'b0, controlled_buffer_1_out} : 3'bz;  // Controlled_Buffer controlled_buffer_5
  assign controlled_buffer_1_out = ry ? instreg_q[6:5] : 2'bz;  // Controlled_Buffer controlled_buffer_6
  assign cc = ccoe ? {instreg_q_3, instreg_q_2} : 4'bz;  // Controlled_Buffer controlled_buffer_7
  and and_1 (and_1_out, ~instreg_q[15], instreg_q[14], ~instreg_q[13], ~instreg_q[12], ~instreg_q[11]);  // AND_Gate
  and and_2 (and_2_out, and_1_out, aop);
  assign OpBus = and_2_out ? multiplexer_1_out : 5'bz;  // Controlled_Buffer controlled_buffer_8
  Multiplexer #(.enable("true"), .select(2), .width(5)) multiplexer_1 (
    .in0(5'b01000), .in1(5'b01010), .in2(5'b01011), .in3(5'b01100), .out(multiplexer_1_out),
    .sel(instreg_q_3), .en(and_1_out));
  fsm fsm_1 (
    .OP(instreg_q[15:11]), .CLK(clk), .CLR(clr), .cTrue(ctrue), .CTest(ctest),
    .signals({ibwrite, ibread, mdrget, mdrput, mdroe, mdrce, maroe, marce, ctest, irce, coe, aop, anop, asub, aadd, si9, si7, ui9, ui7, ui4, frce, froe, lroe, spoe, pcoe, regr, regw, ccoe, ry, rx, rd, t2ce, t2oe, t1ce, t1oe}));
  assign controlled_buffer_4_out = spoe ? 3'b101 : 3'bz;  // Controlled_Buffer controlled_buffer_9
  assign controlled_buffer_10_out = ui7 ? {{9{1'b0}}, instreg_q[6:0]} : 16'bz;  // Controlled_Buffer controlled_buffer_10
  assign controlled_buffer_4_out = lroe ? 3'b110 : 3'bz;  // Controlled_Buffer controlled_buffer_11
  assign controlled_buffer_10_out = ui9 ? {{7{1'b0}}, instreg_q_2, instreg_q[6:0]} : 16'bz;  // Controlled_Buffer controlled_buffer_12
  assign controlled_buffer_10_out = ui4 ? {{12{1'b0}}, instreg_q[3:0]} : 16'bz;  // Controlled_Buffer controlled_buffer_13
  assign OpBus = aadd ? 5'b00001 : 5'bz;  // Controlled_Buffer controlled_buffer_14
  assign OpBus = anop ? {5{1'b0}} : 5'bz;  // Controlled_Buffer controlled_buffer_15
  assign OpBus = asub ? 5'b00010 : 5'bz;  // Controlled_Buffer controlled_buffer_16
  assign controlled_buffer_10_out = si7 ? {{10{instreg_q[6]}}, instreg_q[5:0]} : 16'bz;  // Controlled_Buffer controlled_buffer_17
  assign controlled_buffer_10_out = si9 ? {{8{instreg_q_2[1]}}, instreg_q_2[0], instreg_q[6:0]} : 16'bz;  // Controlled_Buffer controlled_buffer_18
  reg16 instreg (
    .OE(not_2_out), .CE(irce), .CLK(iclk), .D(controlled_buffer_10_out), .CLR(clr),
    .Q({instreg_q[15:11], instreg_q_3, instreg_q_2, instreg_q[6:0]}));
  not not_2 (not_2_out, irce);
  RAM #(.addrWidth(3), .asyncread("true"), .clearpin("true"), .dataWidth(16), .databus("bidir")) registers (
    .addr(controlled_buffer_4_out), .we(regw), .oe(regr), .clk(iclk), .data(controlled_buffer_10_out),
    .clr(clr));
  assign controlled_buffer_10_out = coe ? 16'h1 : 16'bz;  // Controlled_Buffer controlled_buffer_19
  reg16 reg16_1 (.OE(t1oe), .CE(t1ce), .CLK(iclk), .D(controlled_buffer_10_out), .CLR(clr), .Q(reg16_1_q));
  alu alu_1 (
    .Op(OpBus[3:0]), .A(reg16_1_q), .B(controlled_buffer_10_out), .Z(alu_1_c[3]), .C(alu_1_c[0]),
    .V(alu_1_c[1]), .N(alu_1_c[2]), .R(alu_1_r));
  reg16 reg16_2 (.OE(t2oe), .CE(t2ce), .CLK(iclk), .D(alu_1_r), .CLR(clr), .Q(controlled_buffer_10_out));
  ccEval cceval_1 (.cc(cc), .C(reg4_1_q[0]), .V(reg4_1_q[1]), .N(reg4_1_q[2]), .Z(reg4_1_q[3]), .cTrue(ctrue));
  reg4 reg4_1 (.OE(froe), .CE(frce), .CLK(iclk), .D(alu_1_c), .CLR(clr), .Q(reg4_1_q));
  assign controlled_buffer_20_out = mdrput ? controlled_buffer_10_out : 16'bz;  // Controlled_Buffer controlled_buffer_20
  assign controlled_buffer_10_out = mdrget ? mdr_q : 16'bz;  // Controlled_Buffer controlled_buffer_21
  reg16 mdr (.OE(mdroe), .CE(mdrce), .CLK(iclk), .D(controlled_buffer_20_out), .CLR(clr), .Q(mdr_q));
  assign controlled_buffer_22_out = ibwrite ? mdr_q : 16'bz;  // Controlled_Buffer controlled_buffer_22
  assign controlled_buffer_20_out = ibread ? controlled_buffer_22_out : 16'bz;  // Controlled_Buffer controlled_buffer_23
  reg16 mar (.OE(maroe), .CE(marce), .CLK(iclk), .D(controlled_buffer_10_out), .CLR(clr), .Q(mar_q));
  RAM #(.addrWidth(16), .asyncread("true"), .dataWidth(16), .databus("bidir")) ram_1 (
    .addr(mar_q), .we(ibwrite), .oe(ibread), .clk(iclk), .data(controlled_buffer_22_out));

  // Notes on the sheet:
  //   Detect shift/rotate op
endmodule

module alu (
  input  [3:0] Op,
  input  [15:0] A,
  input  [15:0] B,
  output [15:0] R,
  output Z,
  output C,
  output V,
  output N
);

  wire addc, or_3_out, or_4_out, seventeen_out, subb, zero_out;
  wire [2:0] divf, mulf;
  wire [2:1] addf, subf;
  wire [4:0] bitadder_1_out;
  wire [7:0] divq, divrem;
  wire [14:0] addr, divr, mulr, subr;
  wire [15:0] and_1_out, mulc, mulv, not_1_out, not_2_out, or_1_out, shifter_1_out, shifter_2_out,
       shifter_3_out, shifter_4_out;

  Multiplier #(.mode("twosComplement"), .width(16)) multiplier_1 (.a(A), .b(B), .cout(mulv));  // open: out, cin
  xor xor_1 (addf[1], addc, addf[2]);
  xor xor_2 (subf[1], subb, subf[2]);
  assign not_1_out = ~B;  // NOT_Gate not_1, 16 bits wide
  Adder #(.width(16)) adder_1 (.a(A), .b(B), .out({addf[2], addr}), .cin(1'b0), .cout(addc));
  Adder #(.width(16)) adder_2 (.a(A), .b(not_1_out), .out({subf[2], subr}), .cin(1'b1), .cout(subb));
  Multiplier #(.width(16)) multiplier_2 (.a(A), .b(B), .out({mulf[2], mulr}), .cout(mulc));  // open: cin
  Divider #(.width(16)) divider_1 (
    .a(A), .b(B), .out({divq, divr[7:0]}), .rem({divrem, divf[2], divr[14:8]}));  // open: upper
  assign and_1_out = A & B;  // AND_Gate and_1, 16 bits wide
  assign or_1_out = A | B;  // OR_Gate or_1, 16 bits wide
  assign not_2_out = ~B;  // NOT_Gate not_2, 16 bits wide
  Shifter #(.width(16)) shifter_1 (.in(A), .\dist (B[3:0]), .out(shifter_1_out));
  Shifter #(.shift("lr"), .width(16)) shifter_2 (.in(A), .\dist (B[3:0]), .out(shifter_2_out));
  Shifter #(.shift("rl"), .width(16)) shifter_3 (.in(A), .\dist (B[3:0]), .out(shifter_3_out));
  Shifter #(.shift("rr"), .width(16)) shifter_4 (.in(A), .\dist (B[3:0]), .out(shifter_4_out));
  BitAdder #(.width(17)) bitadder_1 (.in0({mulv, mulf[2]}), .out(bitadder_1_out));
  or or_2 (mulf[0], mulc[7], mulc[0], mulc[1], mulc[2], mulc[3], mulc[4], mulc[5], mulc[6], mulc[8], mulc[9], mulc[10], mulc[11], mulc[12], mulc[13], mulc[14], mulc[15]);
  and seventeen (seventeen_out, bitadder_1_out[0], ~bitadder_1_out[1], ~bitadder_1_out[2], ~bitadder_1_out[3], bitadder_1_out[4]);  // AND_Gate
  nor zero (zero_out, bitadder_1_out[0], bitadder_1_out[1], bitadder_1_out[2], bitadder_1_out[3], bitadder_1_out[4]);
  nor nor_1 (mulf[1], seventeen_out, zero_out);
  Multiplexer #(.select(4), .width(16)) multiplexer_1 (
    .in0({16{1'b0}}), .in1({addf[2], addr}), .in2({subf[2], subr}), .in3({mulf[2], mulr}),
    .in4({divf[2], divr}), .in5(and_1_out), .in6(or_1_out), .in7(not_2_out), .in8(shifter_1_out), .in9(B),
    .in10(shifter_2_out), .in11(shifter_3_out), .in12(shifter_4_out), .out(R), .sel(Op));  // open: in13, in14, in15
  or or_3 (or_3_out, divq[3], divq[0], divq[1], divq[2], divq[4], divq[5], divq[6], divq[7]);
  or or_4 (or_4_out, divrem[3], divrem[0], divrem[1], divrem[2], divrem[4], divrem[5], divrem[6], divrem[7]);
  or or_5 (divf[0], or_3_out, or_4_out);
  Multiplexer #(.select(4), .width(3)) multiplexer_2 (
    .in0(3'b000), .in1({addf, addc}), .in2({subf, subb}), .in3(mulf), .in4({divf[2], 1'b0, divf[0]}),
    .in5(3'b000), .in6(3'b000), .in7(3'b000), .in8(3'b000), .in9(3'b000), .in10(3'b000), .in11(3'b000),
    .out({N, V, C}), .sel(Op));  // open: in12, in13, in14, in15
  nor nor_2 (Z, R[15], R[14], R[13], R[12], R[11], R[10], R[9], R[8], R[7], R[6], R[5], R[4], R[3], R[2], R[1], R[0]);

  // Other names for the same wires on the sheet: addf[0] = addc; addr[15] = addf[2]; divr[15] = divf[2];
  //   mulr[15] = mulf[2]; oper[3:0] = Op; subf[0] = subb; subr[15] = subf[2]

  // Notes on the sheet:
  //   Single source operations use B
  //   Add flag generator
  //   Sub flag generator
  //   Detects if any of the 2's compliment multiplication bits + the MSB of the result are different (XOR)
  //   Logisim XOR used voting behaviour which was not desirable
  //   8b remainder 8b quotient, remainder stored in MSBs
  //   Multiplication flag generator
  //   No operation
  //   Division flag generator
  //   Result MUX
  //   Signed division can be implemented in software by correcting for (negating output appropriately) the signs of the two operands
  //   Due to the complexity of signed division, this ALU will only perform unsigned division (hence 0 for V flag)
  //   Flag MUX
endmodule

module reg16 (
  input  [15:0] D,
  input  CE,
  input  OE,
  input  CLK,
  input  CLR,
  output [15:0] Q
);

  wire [15:0] register_1_q;

  Register #(.width(16)) register_1 (.D(D), .en(CE), .clk(CLK), .Q(register_1_q), .clr(CLR));
  assign Q = OE ? register_1_q : 16'bz;  // Controlled_Buffer controlled_buffer_1
endmodule

// FR
module reg4 (
  input  [3:0] D,
  input  CE,
  input  OE,
  input  CLK,
  input  CLR,
  output [3:0] Q
);

  wire [3:0] register_1_q;

  Register #(.width(4)) register_1 (.D(D), .en(CE), .clk(CLK), .Q(register_1_q), .clr(CLR));
  assign Q = OE ? register_1_q : 4'bz;  // Controlled_Buffer controlled_buffer_1
endmodule

module fsm (
  input  CLK,
  input  CLR,
  input  [4:0] OP,
  input  cTrue,
  input  CTest,
  output [34:0] signals
);

  wire branch_out, decode_state_out;
  wire [7:0] decode_data, multiplexer_1_out, multiplexer_2_out, register_1_q;
  wire [63:0] fsm_data;

  ROM #(.addrWidth(5)) decode (.addr(OP), .data(decode_data));
  Multiplexer #(.width(8)) multiplexer_1 (
    .in0(fsm_data[7:0]), .in1(decode_data), .out(multiplexer_1_out), .sel(decode_state_out));
  Multiplexer #(.width(8)) multiplexer_2 (
    .in0(multiplexer_1_out), .in1({8{1'b0}}), .out(multiplexer_2_out), .sel(branch_out));
  and branch (branch_out, ~cTrue, CTest);  // AND_Gate
  and decode_state (decode_state_out, register_1_q[0], register_1_q[1], ~register_1_q[2], ~register_1_q[3], ~register_1_q[4], ~register_1_q[5], ~register_1_q[6], ~register_1_q[7]);  // AND_Gate
  Register register_1 (.D(multiplexer_2_out), .en(CLK), .clk(CLK), .Q(register_1_q), .clr(CLR));
  ROM #(.dataWidth(64)) fsm (.addr(register_1_q), .data({fsm_data[63:43], signals, fsm_data[7:0]}));

  // Notes on the sheet:
  //   contents of decode (hex, n*v repeats v):
  //   0 6*4 9 4 9 c 0 10 1c 14 21 0 6*7 b 7 a e 20 18 1e 16 24
  //   State F0
  //   Only return to F0 if we're branching but cTrue is false
  //   contents of fsm (hex, n*v repeats v):
  //   840060201 23110000902 14240000003 50400 40022205 80424906 40011400 40022208 81400906 80022806
  //   42011000 82000806 4002120d 20422100 4002120f 22400100 18000911 840000412 23040000013 14040011000
  //   40022215 10024911 40022217 14000911 18000919 84000041a a04002101b 45040000000 4002221d 10024919
  //   4002221f 14000919 18000906 440208022 14000923 40050400 440208025 40110422
endmodule

module ccEval (
  input  C,
  input  V,
  input  N,
  input  Z,
  input  [3:0] cc,
  output cTrue
);

  wire ge, gt, hi, le, lo, ls, lt, ne, pl, vc;

  not not_1 (lo, C);
  not not_2 (pl, N);
  not not_3 (vc, V);
  not not_4 (ne, Z);
  and and_1 (hi, C, ~Z);  // AND_Gate
  or or_1 (ls, ~C, Z);  // OR_Gate
  xnor xnor_1 (ge, N, V);
  not not_5 (lt, ge);
  and and_2 (gt, ge, ~Z);  // AND_Gate
  and and_3 (le, lt, Z);
  Multiplexer #(.select(4)) multiplexer_1 (
    .in0(Z), .in1(ne), .in2(C), .in3(hi), .in4(lo), .in5(ls), .in6(N), .in7(pl), .in8(V), .in9(vc),
    .in10(ge), .in11(lt), .in12(gt), .in13(le), .in14(1'b1), .in15(1'b0), .out(cTrue), .sel(cc));

  // Other names for the same wires on the sheet: eq = Z; hs = C; mi = N; vs = V

  // Notes on the sheet:
  //   al
  //   dne
endmodule

module stack (
  input  [7:0] selectedregs,
  input  clk,
  input  pop,
  output [2:0] regaddr,
  output regr,
  output regw
);

  wire bitfinder_1_found, nor_1_out;
  wire [2:0] bitfinder_1_index;
  wire [7:0] and_1_out, mask_q, multiplexer_1_out, multiplexer_2_out, multiplexer_3_out, shifter_1_out,
       shifter_2_out;

  Shifter #(.shift("rr")) shifter_1 (.in(multiplexer_3_out), .\dist (3'b001), .out(shifter_1_out));
  Shifter #(.shift("rl")) shifter_2 (.in(multiplexer_3_out), .\dist (3'b001), .out(shifter_2_out));
  Register mask (.D(multiplexer_1_out), .en(clk), .clk(clk), .Q(mask_q), .clr(1'b0));
  Multiplexer #(.width(8)) multiplexer_1 (.in0(shifter_1_out), .in1(shifter_2_out), .out(multiplexer_1_out), .sel(pop));
  nor nor_1 (nor_1_out, mask_q[7], mask_q[6], mask_q[5], mask_q[4], mask_q[3], mask_q[2], mask_q[1], mask_q[0]);
  Multiplexer #(.width(8)) multiplexer_2 (.in0(8'h1), .in1(8'h80), .out(multiplexer_2_out), .sel(pop));
  Multiplexer #(.width(8)) multiplexer_3 (
    .in0(mask_q), .in1(multiplexer_2_out), .out(multiplexer_3_out), .sel(nor_1_out));
  assign and_1_out = selectedregs & multiplexer_3_out;  // AND_Gate and_1, 8 bits wide
  BitFinder bitfinder_1 (.in(and_1_out), .index(bitfinder_1_index), .found(bitfinder_1_found));
  assign regaddr = bitfinder_1_found ? bitfinder_1_index : 3'bz;  // Controlled_Buffer controlled_buffer_1
  and and_2 (regr, bitfinder_1_found, ~pop);  // AND_Gate
  and and_3 (regw, bitfinder_1_found, pop);

  // Notes on the sheet:
  //   FR, LR, SP, PC, R3-R0
  //   TODO: Determine how to implement FR
  //   one-hot
endmodule
